// Logisim project Single_Cycle_CPU.circ as structural Verilog: 1 circuit, main circuit main
module main (
);

  wire ALUSrc, and_1_out, and_2_out, BneOrBeq, Branch, Clk, clock_1_out, Equal, ExRegWrite, Halt, HasExp,
       IsCOP0, isJAL, isJR, IsRet, IsShamt, IsSyscall, Jump, MemtoReg, multiplexer_4_out, multiplexer_7_out,
       not_2_out, not_3_out, not_4_out, not_5_out, or_1_out, RegWrite, undriven_2, xor_1_out;
  wire [3:0] syscall_decoder_1_hex_2, syscall_decoder_1_hex_3, syscall_decoder_1_hex_4,
       syscall_decoder_1_hex_5;
  wire [15:0] syscall_decoder_1_hex;
  wire [31:0] adder_1_out, adder_2_out, bit_extender_1_out, multiplexer_1_out, multiplexer_3_out,
       multiplexer_6_out, multiplexer_8_out, multiplexer_9_out, multiplexer_10_out, multiplexer_11_out,
       multiplexer_12_out, multiplexer_13_out, ram_1_dout, regfile_1_r1, regfile_1_r2, register_2_q,
       shifter_1_out, undriven, undriven_3, undriven_4, undriven_5, undriven_6;

  Multiplexer #(.width(32)) multiplexer_1 (.in1(undriven), .out(multiplexer_1_out), .sel(and_1_out));  // open: in0
  and and_1 (and_1_out, IsRet, IsCOP0);
  Multiplexer multiplexer_2 (.in0(clock_1_out), .in1(1'b0), .out(Clk), .sel(Halt));
  Clock clock_1 (.out(clock_1_out));
  Multiplexer #(.width(32)) multiplexer_3 (
    .in0({32{1'b0}}), .in1(multiplexer_1_out), .out(multiplexer_3_out), .sel(HasExp));
  not not_1 (HasExp, undriven_2);
  or or_1 (or_1_out, undriven_2, and_1_out);
  Register #(.width(32)) register_1 (.D(multiplexer_3_out), .clk(multiplexer_4_out));  // open: en, Q, clr
  Multiplexer multiplexer_4 (.in0(Clk), .in1(not_2_out), .out(multiplexer_4_out), .sel(or_1_out));
  not not_2 (not_2_out, Clk);
  // control_unit control_unit_1: pin names not known
  Adder #(.width(32)) adder_1 (.b({32{1'b0}}), .out(adder_1_out));  // open: a, cin, cout
  Register #(.width(32)) register_2 (.Q(register_2_q), .clk(HasExp));  // open: D, en, clr
  // CP0 cp0_1: pin names not known; wires that end beside it: Clk, HasExp, ExRegWrite
  Multiplexer #(.width(32)) multiplexer_5 (.in0(undriven_3), .in1(multiplexer_6_out), .sel(not_3_out));  // open: out
  not not_3 (not_3_out, IsCOP0);
  not not_4 (not_4_out, isJAL);
  Multiplexer #(.width(32)) multiplexer_6 (
    .in0(adder_1_out), .in1(multiplexer_12_out), .out(multiplexer_6_out), .sel(not_4_out));
  Multiplexer multiplexer_7 (.in0(RegWrite), .in1(ExRegWrite), .out(multiplexer_7_out), .sel(IsCOP0));
  regfile regfile_1 (.R1(regfile_1_r1), .R2(regfile_1_r2));  // open: R1A, R2A, RW, Din, we, clk, a0, v0
  Multiplexer #(.width(32)) multiplexer_8 (.in0(regfile_1_r2), .in1(undriven_4), .out(multiplexer_8_out), .sel(ALUSrc));
  Bit_Extender #(.in_width(5), .out_width(32), .\type ("zero")) bit_extender_1 (.out(bit_extender_1_out));  // open: in
  Multiplexer #(.width(32)) multiplexer_9 (
    .in0(regfile_1_r1), .in1(undriven_6), .out(multiplexer_9_out), .sel(IsShamt));
  Multiplexer #(.width(32)) multiplexer_10 (
    .in0(multiplexer_8_out), .in1(bit_extender_1_out), .out(multiplexer_10_out), .sel(IsShamt));
  syscall_decoder syscall_decoder_1 (
    .clk(Clk), .Enable(IsSyscall), .v0(regfile_1_r1), .a0(undriven_6), .Halt(Halt),
    .Hex({syscall_decoder_1_hex_5, syscall_decoder_1_hex_4, syscall_decoder_1_hex_3, syscall_decoder_1_hex_2, syscall_decoder_1_hex}));
  // alu alu_1: pin names not known; wires that end beside it: multiplexer_10_out
  RAM #(.dataWidth(32)) ram_1 (.addr(undriven_5[7:0]), .din(undriven_6), .dout(ram_1_dout));  // open: we, oe, clk
  Shifter #(.width(32)) shifter_1 (.in(undriven_4), .\dist ({5{1'b0}}), .out(shifter_1_out));
  xor xor_1 (xor_1_out, Equal, BneOrBeq);
  Hex_Digit_Display hex_digit_display_1 (.value(syscall_decoder_1_hex_5));  // open: dp
  Hex_Digit_Display hex_digit_display_2 (.value(syscall_decoder_1_hex_4));  // open: dp
  Adder #(.width(32)) adder_2 (.b(shifter_1_out), .out(adder_2_out));  // open: a, cin, cout
  Hex_Digit_Display hex_digit_display_3 (.value(syscall_decoder_1_hex_3));  // open: dp
  Hex_Digit_Display hex_digit_display_4 (.value(syscall_decoder_1_hex_2));  // open: dp
  and and_2 (and_2_out, Branch, xor_1_out);
  Hex_Digit_Display hex_digit_display_5 (.value(syscall_decoder_1_hex[15:12]));  // open: dp
  Hex_Digit_Display hex_digit_display_6 (.value(syscall_decoder_1_hex[11:8]));  // open: dp
  Multiplexer #(.width(32)) multiplexer_11 (.in1(adder_2_out), .out(multiplexer_11_out), .sel(and_2_out));  // open: in0
  not not_5 (not_5_out, Jump);
  Hex_Digit_Display hex_digit_display_7 (.value(syscall_decoder_1_hex[7:4]));  // open: dp
  Hex_Digit_Display hex_digit_display_8 (.value(syscall_decoder_1_hex[3:0]));  // open: dp
  Multiplexer #(.width(32)) multiplexer_12 (
    .in0(undriven_5), .in1(ram_1_dout), .out(multiplexer_12_out), .sel(MemtoReg));
  Multiplexer #(.width(32)) multiplexer_13 (
    .in1(multiplexer_11_out), .out(multiplexer_13_out), .sel(not_5_out));  // open: in0
  Multiplexer #(.width(32)) multiplexer_14 (.in0(multiplexer_13_out), .in1(regfile_1_r1), .sel(isJR));  // open: out
  // Pins of 8 and 32 bits meet at undriven_5

  // Notes on the sheet:
  //   PC Buffer
endmodule
